// Logisim project 4 bit binary Arithmetic calculator.circ as structural Verilog: 1 circuit, main circuit main
module main (
  input  Cin,
  input  [1:0] in_2,
  input  [1:0] in_3,
  input  [3:0] A,
  input  [3:0] B,
  output [3:0] out_6,
  output out_7
);

  wire adder_1_cout, adder_2_cout, adder_3_cout, multiplexer_1_out, multiplexer_2_out, multiplexer_3_out,
       multiplexer_4_out, not_1_out, not_2_out, not_3_out, not_4_out, not_5_out, not_6_out, not_7_out,
       not_8_out, xor_1_out, xor_2_out, xor_3_out, xor_4_out;
  wire [3:0] adder_1_out, divider_1_out, multiplier_1_out;

  not not_1 (not_1_out, B[0]);
  xor xor_1 (xor_1_out, B[0], B[0]);
  not not_2 (not_2_out, xor_1_out);
  not not_3 (not_3_out, B[1]);
  xor xor_2 (xor_2_out, B[1], B[1]);
  not not_4 (not_4_out, xor_2_out);
  not not_5 (not_5_out, B[2]);
  xor xor_3 (xor_3_out, B[2], B[2]);
  not not_6 (not_6_out, xor_3_out);
  not not_7 (not_7_out, B[3]);
  xor xor_4 (xor_4_out, B[3], B[3]);
  not not_8 (not_8_out, xor_4_out);
  Multiplexer #(.select(2)) multiplexer_1 (
    .in0(B[0]), .in1(not_1_out), .in2(xor_1_out), .in3(not_2_out), .out(multiplexer_1_out), .sel(in_2));  // open: en
  Multiplexer #(.select(2)) multiplexer_2 (
    .in0(B[1]), .in1(not_3_out), .in2(xor_2_out), .in3(not_4_out), .out(multiplexer_2_out), .sel(in_2));  // open: en
  Multiplexer #(.select(2)) multiplexer_3 (
    .in0(B[2]), .in1(not_5_out), .in2(xor_3_out), .in3(not_6_out), .out(multiplexer_3_out), .sel(in_2));  // open: en
  Multiplexer #(.select(2)) multiplexer_4 (
    .in0(B[3]), .in1(not_7_out), .in2(xor_4_out), .in3(not_8_out), .out(multiplexer_4_out), .sel(in_2));  // open: en
  Adder #(.width(1)) adder_1 (.a(A[0]), .b(multiplexer_1_out), .out(adder_1_out[0]), .cin(Cin), .cout(adder_1_cout));
  Adder #(.width(1)) adder_2 (
    .a(A[1]), .b(multiplexer_2_out), .out(adder_1_out[1]), .cin(adder_1_cout), .cout(adder_2_cout));
  Adder #(.width(1)) adder_3 (
    .a(A[2]), .b(multiplexer_3_out), .out(adder_1_out[2]), .cin(adder_2_cout), .cout(adder_3_cout));
  Adder #(.width(1)) adder_4 (.a(A[3]), .b(multiplexer_4_out), .out(adder_1_out[3]), .cin(adder_3_cout), .cout(out_7));
  Multiplier #(.width(4)) multiplier_1 (.a(A), .b(B), .out(multiplier_1_out));  // open: cin, cout
  Divider #(.width(4)) divider_1 (.a(A), .b(B), .out(divider_1_out));  // open: upper, rem
  Multiplexer #(.select(2), .width(4), .enable("false")) multiplexer_5 (
    .in0(adder_1_out), .in1(adder_1_out), .in2(multiplier_1_out), .in3(divider_1_out), .out(out_6), .sel(in_3));
endmodule
